# Fritzing sketch pencil-measurement-amplified (saved by Fritzing 1.0.1rc)
breadboards: 1

parts:
  Part1 = Arduino Uno (Rev3)
  U1 = LM358 [package=dip08]
  Pencil = Rotary Potentiometer (Small) [maximum_resistance=50Ω knob_status=50% power=0.5W package=THT]
  R3 = Resistor [tolerance=±5% power=0.25W resistance=10k package=THT]
  R4 = Resistor [tolerance=±5% power=0.25W resistance=1k package=THT]
  R7 = Resistor [tolerance=±5% power=0.25W resistance=10k package=THT]
  R8 = Resistor [tolerance=±5% power=0.25W resistance=1k package=THT]
  R10 = Resistor [tolerance=±5% power=0.25W resistance=1k package=THT]
  R11 = Resistor [tolerance=±5% power=0.25W resistance=1k package=THT]

nets:
  N1: Part1.A0, U1.G$1_OUT, R7.Pin_1
  N2: Part1.A1, U1.G$2_OUT, R3.Pin_0
  5V: Part1.5V, U1.G$1_V+, R10.Pin_1, R11.Pin_1
  GND: Part1.GND, U1.G$1_V-, Pencil.wiper, R4.Pin_0, R8.Pin_1
  N3: U1.G$1_-IN, R7.Pin_0, R8.Pin_0
  N4: U1.G$1_+IN, Pencil.leg2, R11.Pin_0
  N5: U1.G$2_+IN, Pencil.leg1, R10.Pin_0
  N6: U1.G$2_-IN, R3.Pin_1, R4.Pin_1
